# Fritzing sketch sketch (saved by Fritzing 0.9.3b)
breadboards: 1

parts:
  Part2 = Real Time Clock Module - DS1307 RTC Breakout Board
  J1 = Piezo Speaker
  S5 = Pushbutton [package="[THT]"]
  S6 = Pushbutton [package="[THT]"]
  S7 = Pushbutton [package="[THT]"]
  S8 = Pushbutton [package="[THT]"]
  hc-sr1 = hc-sr04
  Part3 = Arduino Uno (Rev3) - ICSP
  R2 = Resistor [tolerance=±5% resistance=220 package="0402 [SMD]"]
  R3 = Resistor [tolerance=±5% resistance=220 package="0402 [SMD]"]
  R4 = Resistor [tolerance=±5% resistance=220 package="0402 [SMD]"]
  R5 = Resistor [tolerance=±5% resistance=220 package="0402 [SMD]"]
  R6 = Resistor [tolerance=±5% resistance=220 package="0402 [SMD]"]
  U1 = Nokia 6100 Color LCD [package=nokia6100_lcd]

nets:
  5V: Part2.5V, S5.Pin_2, S6.Pin_2, S7.Pin_2, S8.Pin_1, S8.Pin_2, hc-sr1.VCC, Part3.5V, U1.LEDGND
  GND: Part2.GND, hc-sr1.GND, Part3.GND, R2.Pin_1, R3.Pin_1, R4.Pin_1, R5.Pin_1, R6.Pin_1, U1.VLED
  N1: Part2.SQW, Part3.A4/SDA
  N2: Part2.SCL, Part3.A5/SCL
  N3: J1.pin1, R6.Pin_0
  N4: J1.pin2, Part3.D7
  N5: S5.Pin_4, Part3.A0, R2.Pin_0
  N6: S6.Pin_4, R3.Pin_0
  N7: S7.Pin_4, R5.Pin_0
  N8: S8.Pin_4, R4.Pin_0
  N9: hc-sr1.Trig, Part3.D5_PWM
  N10: hc-sr1.Echo, Part3.D6_PWM
  N11: Part3.D8, U1.SCK
  N12: Part3.D9_PWM, U1.DIO
  N13: Part3.D10_PWM/SS, U1.CS
  N14: Part3.D11_PWM/MOSI, U1.RESET
  N15: Part3.D13/SCK, U1.VDIGITAL

notes:
  GND, VCC
  SCL, SDA, RES, DC, CS
