# Fritzing sketch sketch (saved by Fritzing 0.9.3b)
breadboards: 4

parts:
  Part1 = Arduino Uno (Rev3)
  Disp1 = LBT2088AH [part_number=LBT2088AH]  # not connected
  U1 = MAX7219 [package=dil24]
  R1 = Resistor [tolerance=±5% resistance=10k package=THT]  # not connected
  R2 = Resistor [tolerance=±5% resistance=10k package=THT]  # not connected
  R3 = Resistor [tolerance=±5% resistance=10k package=THT]  # not connected

nets:
  N1: Part1.D10_PWM/SS, U1.LOAD
  N2: Part1.D11_PWM/MOSI, U1.DIN
  N3: Part1.D13/SCK, U1.CLK
  5V: Part1.5V, U1.VCC
  GND: Part1.GND, U1.GND, U1.GND2

notes:
  9-16
  1-8
  Modellnummer / Hakk
  Denne siden.
